# Fritzing sketch capibara_arduino_nano_esp32 (saved by Fritzing 1.0.2b)
breadboards: 1

parts:
  A1 = Arduino Nano ESP32
  Part1 = GMT020-02 TFT Display
  S1 = Pushbutton [package="[THT]"]
  S2 = Pushbutton [package="[THT]"]
  S3 = Pushbutton [package="[THT]"]
  S4 = Pushbutton [package="[THT]"]
  S5 = Pushbutton [package="[THT]"]
  Part2 = PN532 Elechouse RFID NFC Module V3
  SD_card_module1 = SD Card Module

nets:
  N1: A1.Pin_1, Part1.SCL(SCLK)
  N2: A1.Pin_2, Part1.3.3V, SD_card_module1.+3.3
  N3: A1.Pin_5, S1.Pin_1, S1.Pin_2
  N4: A1.Pin_6, A1.Pin_14, A1.Pin_19, Part1.GND, S1.Pin_3, S1.Pin_4, S2.Pin_3, S2.Pin_4, S3.Pin_3, S3.Pin_4, S4.Pin_3, S4.Pin_4, S5.Pin_3, S5.Pin_4, SD_card_module1.GND#0
  N5: A1.Pin_7, S5.Pin_1, S5.Pin_2
  N6: A1.Pin_8, Part2.SCL
  N7: A1.Pin_9, Part2.SDA
  N8: A1.Pin_10, S2.Pin_1, S2.Pin_2
  N9: A1.Pin_11, S4.Pin_1, S4.Pin_2
  N10: A1.Pin_20, SD_card_module1.MISO
  N11: A1.Pin_21, SD_card_module1.SCK
  N12: A1.Pin_22, SD_card_module1.MOSI
  N13: A1.Pin_23, SD_card_module1.CS
  N14: A1.Pin_27, Part1.CS
  N15: A1.Pin_28, Part1.DC
  N16: A1.Pin_29, Part1.RST
  N17: A1.Pin_30, Part1.SDA(MOSI)
  N18: S3.Pin_1, S3.Pin_2

custom parts:
  Arduino Nano ESP32: Arduino® Nano ESP32 tht.
  GMT020-02 TFT Display: TFT Display 240x320 with ST7789 or compatible driver, SPI bus. This part is made from Adafruit ST7789 2.0 display.
  PN532 Elechouse RFID NFC Module V3: NFC is a popular technology in recent years. We often heard this work while smart phone company such as Samsung or HTC introduces their latest high-end phones. Almost all the high-end phone in the market support NFC. Near field communication (NFC) is a set of standards for smart phones and similar devices to establish radio communication with each other by touching them together or bringing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
  SD Card Module: SD Card Module Slot Socket Reader For Arduino ARM MCU
